# Fritzing sketch penyiramandanpengkabutan (saved by Fritzing 0.9.5d)

parts:
  A1 = ESP32 devkit 38p expansion board
  MH-ET_LIVE_ESP32_DEVKIT1 = MH-ET LIVE ESP32 DEVKIT 38 pins  # not connected
  DHT1 = DHT11 Humitidy and Temperature Sensor (3 pins)
  PART1 = SparkFun Soil Moisture Sensor [part_number=SEN-13322]
  U1 = 2-Channel 5v Relay Shield [package=relay-2ch5v10a]
  J1 = Camdenboss CTB0158-2 [part_number=CTB0158-2 package=THT]
  J2 = Camdenboss CTB0158-2 [part_number=CTB0158-2 package=THT]
  WATER_PUMP1 = water pump/motor
  WATER_PUMP2 = water pump/motor

nets:
  N1: A1.Pin_7, PART1.SIG
  VCC: A1.Pin_17, A1.Pin_56, A1.Pin_57, A1.Pin_98, DHT1.Plus, PART1.VCC, U1.VCC
  GND: A1.Pin_52, A1.Pin_53, A1.Pin_124, A1.Pin_144, DHT1.Gnd, PART1.GND, U1.GND
  N2: A1.Pin_168, DHT1.Signal
  N3: A1.Pin_177, U1.IN2
  N4: A1.Pin_178, U1.IN1
  N5: U1.K1-In, J1.terminal_2, WATER_PUMP1.pin_2
  N6: U1.K1-On, J1.terminal_1, WATER_PUMP1.pin_1
  N7: U1.K2-In, J2.terminal_2, WATER_PUMP2.pin_2
  N8: U1.K2-On, J2.terminal_1, WATER_PUMP2.pin_1

notes:
  SOIL HUMIDITY MOISTURE
  DHT11
  RELAY 2 CHANNEL
  ESP-32 DOIT WIFI BOARD 38 PIN
  BLOK TERMINAL 2 PIN
  POMPA AIR

custom parts:
  ESP32 devkit 38p expansion board: Upgraded ESP32 38P Development ESP32-DevKitC-32 ESP-WROOM-32 Expansion Board.
  MH-ET LIVE ESP32 DEVKIT 38 pins: http://mh.nodebb.com/topic/2/mh-et-live-esp32-devkit
  DHT11 Humitidy and Temperature Sensor (3 pins): DHT11 Humidity and Temperature Sensor (3 pins).
  SparkFun Soil Moisture Sensor: The SparkFun Soil Moisture Sensor is a simple breakout for measuring the moisture in soil and similar materials.
  2-Channel 5v Relay Shield: 2 Channel 5v Relay Shield w. 2x SPD-06VDC-SD-C
  water pump/motor: WATER PUMP BY ARDUBLOCKTR
